// Logisim project ID_EX_buffer.circ as structural Verilog: 1 circuit, main circuit ID_EX
module ID_EX (
  input  clk,
  input  [31:0] PC,
  input  [31:0] RD1,
  input  [31:0] RD2,
  input  [31:0] Ext,
  input  [4:0] instr1,
  input  [4:0] instr2,
  input  RegDes,
  input  AluSrc,
  input  [5:0] AluOp,
  input  Branch,
  input  [3:0] MemMask,
  input  MemToReg,
  input  JAL,
  input  RegWrite,
  input  [4:0] func,
  input  [4:0] sh_amount,
  input  [5:0] opcode,
  output [31:0] n_PC,
  output [31:0] n_RD1,
  output [31:0] n_RD2,
  output [31:0] n_Ext,
  output [4:0] n_instr1,
  output [4:0] n_instr2,
  output n_RegDes,
  output n_AluSrc,
  output [5:0] n_AluOp,
  output n_Branch,
  output [3:0] n_MemMask,
  output n_MemToReg,
  output n_JAL,
  output n_RegWrite,
  output [4:0] n_sh_amount,
  output [4:0] n_func,
  output [5:0] n_opcode
);

  Register #(.width(32)) register_1 (.D(PC), .en(1'b1), .clk(clk), .Q(n_PC));  // open: clr
  Register #(.width(32)) register_2 (.D(RD1), .en(1'b1), .clk(clk), .Q(n_RD1));  // open: clr
  Register #(.width(32)) register_3 (.D(RD2), .en(1'b1), .clk(clk), .Q(n_RD2));  // open: clr
  Register #(.width(32)) register_4 (.D(Ext), .en(1'b1), .clk(clk), .Q(n_Ext));  // open: clr
  Register #(.width(5)) register_5 (.D(instr1), .en(1'b1), .clk(clk), .Q(n_instr1));  // open: clr
  Register #(.width(5)) register_6 (.D(instr2), .en(1'b1), .clk(clk), .Q(n_instr2));  // open: clr
  Register #(.width(1)) register_7 (.D(RegDes), .en(1'b1), .clk(clk), .Q(n_RegDes));  // open: clr
  Register #(.width(1)) register_8 (.D(AluSrc), .en(1'b1), .clk(clk), .Q(n_AluSrc));  // open: clr
  Register #(.width(6)) register_9 (.D(AluOp), .en(1'b1), .clk(clk), .Q(n_AluOp));  // open: clr
  Register #(.width(1)) register_10 (.D(Branch), .en(1'b1), .clk(clk), .Q(n_Branch));  // open: clr
  Register #(.width(1)) register_11 (.D(MemToReg), .en(1'b1), .clk(clk), .Q(n_MemToReg));  // open: clr
  Register #(.width(1)) register_12 (.D(JAL), .en(1'b1), .clk(clk), .Q(n_JAL));  // open: clr
  Register #(.width(4)) register_13 (.D(MemMask), .en(1'b1), .clk(clk), .Q(n_MemMask));  // open: clr
  Register #(.width(1)) register_14 (.D(RegWrite), .en(1'b1), .clk(clk), .Q(n_RegWrite));  // open: clr
  Register #(.width(5)) register_15 (.D(func), .en(1'b1), .clk(clk), .Q(n_func));  // open: clr
  Register #(.width(5)) register_16 (.D(sh_amount), .en(1'b1), .clk(clk), .Q(n_sh_amount));  // open: clr
  Register #(.width(6)) register_17 (.D(opcode), .en(1'b1), .clk(clk), .Q(n_opcode));  // open: clr

  // Notes on the sheet:
  //   inputs
  //   outputs
endmodule
