// Logisim project IF_ID.circ as structural Verilog: 1 circuit, main circuit Instruction_Fetch
module Instruction_Fetch (
  input  clk,
  input  [31:0] PC,
  input  [31:0] instr,
  output [31:0] n_PC,
  output [31:0] n_instr
);

  Register #(.width(32)) register_1 (.D(PC), .en(1'b1), .clk(clk), .Q(n_PC));  // open: clr
  Register #(.width(32)) register_2 (.D(instr), .en(1'b1), .clk(clk), .Q(n_instr));  // open: clr

  // Notes on the sheet:
  //   inputs
  //   outputs
endmodule
