// Logisim project cpu.circ as structural Verilog: 1 circuit, main circuit cpu
module cpu (
  input  in_1,
  input  [3:0] in_2,
  input  [31:0] in_3,
  input  in_4
);

  wire ALUOpValid, ALUSrc, ALUSrc_EX, and_3_out, and_4_out, and_5_out, and_6_out, and_7_out, Branch,
       Branch_MEM, cacheWrite, clk, comparator_1_eq, comparator_2_eq, CPUclk, En1, En2, ex_mem_1_n_jal,
       ex_mem_1_n_memtoreg, ex_mem_1_n_regwrite, id_ex_1_p28, id_ex_1_p30, id_ex_1_p31, id_ex_1_p32, is_op,
       JAL, JAL_WB, Jump, JumpReg, LB, MemToReg, MemToReg_MEM, memWrite, miss, multiplexer_2_out,
       multiplexer_4_out, nor_1_out, not_1_out, not_2_out, not_3_out, not_4_out, not_5_out, not_6_out,
       not_7_out, not_8_out, not_9_out, not_10_out, not_11_out, not_12_out, not_13_out, not_14_out, RegDes,
       RegDes_EX, RegWrite, RegWrite_WB, SLTi, syscall, undriven, validMiss, zero, zero_MEM;
  wire [3:0] counter_1_q, counter_2_q, id_ex_1_p29, MemMask, MemMask_MEM, memtocache_1_memmask;
  wire [4:0] ex_mem_1_n_write, instr1_EX, instr2, instr2_EX, instr3, multiplexer_5_out, sh_amount_EX,
       undriven_2, Write, Write_WB;
  wire [5:0] ALUOp, ALUOp_EX, func, func_EX, opcd_fnc, opcode_EX;
  wire [13:0] cache_1_p11;
  wire [15:2] MemAddr;
  wire [15:6] instr0;
  wire [31:0] added_PC, added_PC_MEM, Data_WB, ex_mem_1_n_pc, ex_mem_1_n_rd2, ex_mem_1_n_result, extended,
       extended_EX, final_writeData, id_ex_1_p19, id_ex_1_p21, instr, instr_ID, MemData, memData_t,
       memtocache_1_word, memWriteData, multiplexer_6_out, multiplexer_8_out, multiplexer_10_out, n_PC_IF,
       new_PC, PC, PC_ID, PC_IF, PC_WB, rdData1, rdData1_EX, rdData2, result, result_WB, shifter_1_out,
       undriven_3, W0, w0_t, W1, w1_t, W2, w2_t, W3, w3_t, writeData;
  wire [31:26] n_instr;

  not not_1 (not_1_out, syscall);
  Register #(.width(32)) register_1 (.D(new_PC), .en(not_1_out), .clk(CPUclk), .Q(PC), .clr(1'b1));
  not not_2 (not_2_out, validMiss);
  Adder #(.width(32)) adder_1 (.a(PC), .b(32'h4), .out(PC_IF), .cin(1'b0));  // open: cout
  Clock clock_1 (.out(clk));
  and and_1 (En1, miss, validMiss);
  and and_2 (En2, miss, not_2_out);
  Counter #(.max('hf), .width(4)) counter_1 (
    .count(En2), .Q(counter_1_q), .up(1'b1), .clk(clk), .clr(comparator_2_eq));  // open: load, D, carry
  Counter #(.max('hf), .width(4)) counter_2 (
    .D(4'b0000), .count(En1), .Q(counter_2_q), .up(undriven), .clk(clk), .clr(comparator_1_eq));  // open: load, carry
  not not_3 (not_3_out, counter_2_q[1]);
  Comparator #(.width(4)) comparator_1 (.a(counter_2_q), .b(4'b1110), .eq(comparator_1_eq));  // open: gt, lt
  Comparator #(.width(4)) comparator_2 (.a(counter_1_q), .b(4'b1001), .eq(comparator_2_eq));  // open: gt, lt
  not not_4 (not_4_out, counter_1_q[0]);
  not not_5 (not_5_out, counter_1_q[1]);
  not not_6 (not_6_out, counter_1_q[2]);
  // mem mem_1: pin names not known; wires that end beside it: PC, in_2, in_3, CPUclk, instr
  and and_3 (and_3_out, not_4_out, not_5_out, clk, not_6_out, counter_1_q[3]);
  and and_4 (and_4_out, counter_2_q[0], not_3_out, counter_2_q[2], counter_2_q[3], clk);
  Multiplexer #(.width(32)) multiplexer_1 (
    .in0(writeData), .in1({rdData2[31:8], writeData[7:0]}), .out(final_writeData), .sel(LB));
  IF_ID if_id_1 (.clk(CPUclk), .PC(PC_IF), .instr(instr), .n_PC(PC_ID), .n_instr(instr_ID));
  Multiplexer multiplexer_2 (.in0(and_3_out), .in1(and_4_out), .out(multiplexer_2_out), .sel(validMiss));
  Shifter #(.width(32)) shifter_1 (.in(extended), .\dist (5'b00010), .out(shifter_1_out));
  Multiplexer #(.width(5)) multiplexer_3 (.in0(instr2), .in1(instr0[15:11]), .out(Write), .sel(RegDes));
  Multiplexer multiplexer_4 (.in0(clk), .in1(multiplexer_2_out), .out(multiplexer_4_out), .sel(miss));
  Adder #(.width(32)) adder_2 (.a(n_PC_IF), .b(shifter_1_out), .out(added_PC), .cin(1'b0));  // open: cout
  Multiplexer #(.width(5)) multiplexer_5 (.in0(undriven_2), .in1({5{1'b1}}), .out(multiplexer_5_out), .sel(JAL));
  Multiplexer #(.width(32)) multiplexer_6 (.in0(final_writeData), .in1(PC), .out(multiplexer_6_out), .sel(JAL));
  Multiplexer multiplexer_7 (.in0(clk), .in1(multiplexer_4_out), .out(CPUclk), .sel(in_4));
  Multiplexer #(.width(32)) multiplexer_8 (.in0(PC_IF), .in1(undriven_3), .out(multiplexer_8_out), .sel(and_5_out));
  and and_5 (and_5_out, zero, Branch);
  Multiplexer #(.width(32)) multiplexer_9 (
    .in0(multiplexer_8_out), .in1({n_PC_IF[31:28], instr3, instr2, instr0, func, 2'b00}), .out(new_PC),
    .sel(Jump));
  SignExtend signextend_1 (.inpt({instr0, func}), .opcode(n_instr), .outpt(extended));
  // regfile RegisterFile: pin names not known; wires that end beside it: instr3, instr2, multiplexer_6_out, RegWrite, CPUclk, multiplexer_5_out, rdData1, rdData2
  Multiplexer #(.width(32)) multiplexer_10 (.in0(rdData2), .in1(extended), .out(multiplexer_10_out), .sel(ALUSrc));
  // ID_EX id_ex_1: pin names not known; wires that end beside it: CPUclk, PC_ID, rdData1, rdData2, extended, instr0[15:11], instr2, RegDes, ALUSrc, ALUOp, Branch, MemMask, MemToReg, JAL, RegWrite, func, instr0[10:6], n_instr, id_ex_1_p19, rdData1_EX, id_ex_1_p21, extended_EX, instr1_EX, instr2_EX, RegDes_EX, ALUSrc_EX, ALUOp_EX, id_ex_1_p28, id_ex_1_p29, id_ex_1_p30, id_ex_1_p31, id_ex_1_p32, sh_amount_EX, func_EX, opcode_EX
  // ControlUnit controlunit_1: pin names not known; wires that end beside it: n_instr, func, ALUSrc, RegWrite, ALUOp, ALUOpValid, MemMask, JAL, JumpReg, RegDes, Jump, Branch, LB, MemToReg, syscall, SLTi
  aluControl alucontrol_1 (.func(func), .aluOP(ALUOp), .opcd_fnc(opcd_fnc), .is_op(is_op));
  alu alu_1 (
    .rs(rdData1), .rt_imm(multiplexer_10_out), .opcd_fnc(opcd_fnc), .shft_amt(instr0[10:6]), .is_i(is_op),
    .result(result), .zero(zero));
  EX_MEM ex_mem_1 (
    .clk(CPUclk), .PC(id_ex_1_p19), .Result(result), .RD2(id_ex_1_p21), .Write(Write), .Zero(zero),
    .Branch(id_ex_1_p28), .MemMask(id_ex_1_p29), .MemToReg(id_ex_1_p30), .JAL(id_ex_1_p31),
    .RegWrite(id_ex_1_p32), .added_PC(added_PC), .n_Result(ex_mem_1_n_result), .n_PC(ex_mem_1_n_pc),
    .n_RD2(ex_mem_1_n_rd2), .n_Write(ex_mem_1_n_write), .n_Zero(zero_MEM), .n_Branch(Branch_MEM),
    .n_MemMask(MemMask_MEM), .n_MemToReg(ex_mem_1_n_memtoreg), .n_JAL(ex_mem_1_n_jal),
    .n_RegWrite(ex_mem_1_n_regwrite), .n_added_PC(added_PC_MEM));
  Multiplexer #(.width(32)) multiplexer_11 (.in0(result), .in1(MemData), .out(writeData), .sel(MemToReg));
  not not_7 (not_7_out, MemMask[0]);
  not not_8 (not_8_out, MemMask[1]);
  not not_9 (not_9_out, MemMask[2]);
  and and_6 (and_6_out, not_7_out, not_8_out, not_9_out, MemMask[3]);
  Multiplexer #(.width(32)) multiplexer_12 (
    .in0(rdData2), .in1({MemData[31:8], rdData2[7:0]}), .out(memWriteData), .sel(and_6_out));
  MEM_WB mem_wb_1 (
    .clk(CPUclk), .PC(ex_mem_1_n_pc), .Result(ex_mem_1_n_result), .Data(ex_mem_1_n_rd2),
    .Write(ex_mem_1_n_write), .MemToReg(ex_mem_1_n_memtoreg), .JAL(ex_mem_1_n_jal),
    .RegWrite(ex_mem_1_n_regwrite), .n_Result(result_WB), .n_PC(PC_WB), .n_Data(Data_WB), .n_Write(Write_WB),
    .n_MemToReg(MemToReg_MEM), .n_JAL(JAL_WB), .n_RegWrite(RegWrite_WB));
  Multiplexer #(.width(32)) multiplexer_13 (.in0(w0_t), .in1(memData_t), .out(W0), .sel(not_10_out));
  Multiplexer #(.width(32)) multiplexer_14 (.in0(w1_t), .in1(memData_t), .out(W1), .sel(not_10_out));
  Multiplexer #(.width(32)) multiplexer_15 (.in0(w2_t), .in1(memData_t), .out(W2), .sel(not_10_out));
  Multiplexer #(.width(32)) multiplexer_16 (.in0(w3_t), .in1(memData_t), .out(W3), .sel(not_10_out));
  // cache cache_1: pin names not known; wires that end beside it: result[15:2], in_1, clk, cacheWrite, memWriteData, MemData, validMiss, miss, w0_t, w1_t, cache_1_p11, w2_t, w3_t
  not not_10 (not_10_out, memWrite);
  memToCache memtocache_1 (
    .miss(miss), .validmiss(validMiss), .word_0(W0), .word_1(W1), .word_2(W2), .word_3(W3),
    .address_out(cache_1_p11), .clk(clk), .memmask(memtocache_1_memmask), .memwrite(memWrite),
    .word(memtocache_1_word), .address(MemAddr));
  // memDelayed memdelayed_1: pin names not known; wires that end beside it: {{16{1'b0}}, MemAddr, 2'b00}, memtocache_1_memmask, memtocache_1_word, clk, memData_t
  not not_11 (not_11_out, n_instr[27]);
  not not_12 (not_12_out, n_instr[29]);
  not not_13 (not_13_out, n_instr[26]);
  not not_14 (not_14_out, n_instr[28]);
  and and_7 (and_7_out, n_instr[26], not_11_out, n_instr[28], not_12_out, n_instr[30], n_instr[31]);
  nor nor_1 (nor_1_out, not_13_out, n_instr[27], not_14_out, n_instr[29], n_instr[30], n_instr[31]);
  or or_1 (cacheWrite, and_7_out, nor_1_out, memWrite);

  // Other names for the same wires on the sheet: MemToCacheAddr[13:0] = MemAddr; instr0[5:0] = func;
  //   Jinstr[25:0] = {instr3, instr2, instr0, func}; n_instr[25:0] = {instr3, instr2, instr0, func};
  //   sh_amount[4:0] = instr0[10:6]; instr1[4:0] = instr0[15:11]; opcode[5:0] = n_instr
endmodule
