// Logisim project memToCache.circ as structural Verilog: 1 circuit, main circuit memToCache
module memToCache (
  input  miss,
  input  validmiss,
  input  [31:0] word_0,
  input  [31:0] word_1,
  input  [31:0] word_2,
  input  [31:0] word_3,
  input  [13:0] address_out,
  input  clk,
  output [3:0] memmask,
  output memwrite,
  output [31:0] word,
  output [13:0] address
);

  wire and_2_out, miss_t, not_1_out;

  and and_1 (miss_t, miss, validmiss);
  Multiplexer #(.select(2), .width(32), .enable("false")) multiplexer_1 (
    .in0(word_0), .in1(word_1), .in2(word_2), .in3(word_3), .out(word), .sel(address[1:0]));
  and and_2 (and_2_out, address[0], address[1]);
  T_Flip_Flop t_ff_1 (.T(miss_t), .clk(and_2_out), .Q(memwrite), .reset(not_1_out));  // open: Qn, preset
  not not_1 (not_1_out, miss_t);
  MemAddressGen memaddressgen_1 (
    .address(address_out), .miss(miss_t), .clk(clk), .read(miss_t), .memmask(memmask), .memaddress(address));  // open: readmem

  // Other names for the same wires on the sheet: bit0 = address[0]; bit1 = address[1]
endmodule
